# Fritzing sketch Untitled Sketch 2 (saved by Fritzing 0.9.3b)
breadboards: 1

parts:
  R2 = Rotary Potentiometer (Small) [maximum_resistance=10kΩ package=THT]
  Q1 = MOSFET-NCHANNEL [package=to220v]
  Part1 = Arduino Uno (Rev3)
  R3 = Resistor [tolerance=±5% resistance=220 package="2010 [SMD]"]
  C1 = Capacitor [package=cap-pth-small2]
  D1 = Schottky Diode [part_number=1N5817 package="300 mil [THT]"]  # not connected
  L1 = Inductor [package="0603 [SMD]"]
  VCC1 = Battery block 9V

nets:
  N1: R2.leg1, Q1.S, Part1.GND, C1.2, VCC1.-
  N2: R2.wiper, Part1.A0, C1.1
  N3: R2.leg2, Part1.5V
  N4: Q1.G, R3.Pin_1
  N5: Q1.D, L1.pin_0
  N6: Part1.D9_PWM, R3.Pin_0
  N7: L1.pin_1, VCC1.+

notes:
  24V DC
